# Fritzing sketch esp8266_board (saved by Fritzing 0.9.2b)
circuit board: 8.46667cm x 5.64444cm
breadboards: 1

parts:
  Firmware_Update = Momentary Switch [package=ksa_sealed_tac_switch]
  U1 = ESP8266 WiFi Module [part_number=ESP8266]
  Reset = Momentary Switch [package=ksa_sealed_tac_switch]
  R1 = Resistor [tolerance=±5% resistance=10k package=THT]
  R2 = Resistor [tolerance=±5% resistance=10k package=THT]
  R3 = Resistor [tolerance=±5% resistance=10k package=THT]
  C1 = Ceramic Capacitor [capacitance=100nF package="100 mil [THT, multilayer]"]
  C2 = Electrolytic Capacitor [capacitance=0.1mF package="100 mil [THT, electrolytic]"]
  C3 = Ceramic Capacitor [capacitance=100nF package="100 mil [THT, multilayer]"]
  Q1 = NPN-Transistor [package="TO92 [THT]"]
  Q2 = NPN-Transistor [package="TO92 [THT]"]
  R4 = Resistor [tolerance=±5% resistance=10k package=THT]
  R5 = Resistor [tolerance=±5% resistance=10k package=THT]
  R6 = Resistor [tolerance=±5% resistance=470 package=THT]
  R7 = Resistor [tolerance=±5% resistance=470 package=THT]
  R8 = Resistor [tolerance=±5% resistance=0 package=THT]
  LED1 = LEDs [package=led10mm]
  R9 = Resistor [tolerance=±5% resistance=470 package=THT]
  I/O = female pin header, 4 pins [form="♀ (female)"]
  POWER = female pin header, 2 pins [form="♀ (female)"]
  J2 = male pin header, 6 pins [form="♂ (male)"]

nets:
  N1: Firmware_Update.1, Firmware_Update.2, R6.Pin_1
  GND: Firmware_Update.3, Firmware_Update.4, U1.GND, Reset.3, Reset.4, C1.0, C2.-, C3.0, I/O.pin4, POWER.pin2, J2.pin6
  RXD: U1.RXD, J2.pin2
  3.3V: U1.VCC, U1.CH_PD, R1.Pin_0, R2.Pin_0, R3.Pin_0, C2.+, C3.1, R9.Pin_0, I/O.pin1, POWER.pin1, J2.pin1
  GPIO0/IN/Update: U1.GPIO_0, R1.Pin_1, Q2.C, R6.Pin_0, I/O.pin3
  RESET: U1.GPIO_16, R8.Pin_0, LED1.C
  GPIO2/OUT: U1.GPIO_2, R2.Pin_1, I/O.pin2
  TXD: U1.TXD, J2.pin3
  N2: Reset.1, Reset.2, R7.Pin_1, R8.Pin_1
  nRST: R3.Pin_1, C1.1
  RTS: Q1.E, R5.Pin_1, J2.pin4
  N3: Q1.B, R4.Pin_0
  nRTS: Q1.C, R7.Pin_0
  DTR: Q2.E, R4.Pin_1, J2.pin5
  N4: Q2.B, R5.Pin_0
  N5: LED1.A, R9.Pin_1

custom parts:
  ESP8266 WiFi Module: Generic WiFi Module based on the ESP8266 with onboard PCB antenna and UART communications
